# Fritzing sketch 2stageTransistor (saved by Fritzing 0.9.3b)
breadboards: 1

parts:
  Part1 = Arduino Uno (Rev3)
  Q1 = npn-Powertransistor [package="TO220 [THT]"]
  Q2 = npn-Powertransistor [package="TO220 [THT]"]
  U1 = LIPO-2000mAh [package=lipo-2000]
  M1 = DC Motor
  R1 = Resistor [tolerance=±5% resistance=220 package="2010 [SMD]"]
  R2 = Resistor [tolerance=±5% resistance=220 package="2010 [SMD]"]

nets:
  N1: Part1.GND, Q1.emitter, U1.-, R2.Pin_0
  N2: Part1.D3_PWM, Q1.base, R2.Pin_1
  N3: Part1.3V3, Q2.base, R1.Pin_1
  N4: Q1.collector, Q2.emitter, R1.Pin_0
  N5: Q2.collector, M1.pin_1
  N6: U1.+, M1.pin_2
