# Fritzing sketch Lab3Diagram (saved by Fritzing 0.9.2b)
breadboards: 1

parts:
  R1 = Resistor [tolerance=±5% resistance=220 package=THT]
  Q1 = npn-Powertransistor [package="TO220 [THT]"]
  M1 = DC Motor
  U1 = LIPO-2000mAh [package=lipo-2000]

nets:
  N1: R1.Pin_0, Q1.collector
  N2: R1.Pin_1, Q1.emitter, U1.-
  N3: Q1.base, M1.pin_1
  N4: M1.pin_2, U1.+
