# Fritzing sketch Circuit (saved by Fritzing 0.9.2b)
breadboards: 1

parts:
  Part1 = Arduino Due (Rev2b)
  P1 = S1133 Si Photodiode [package="8mm Ceramic [THT]"]
  P2 = S1133 Si Photodiode [package="8mm Ceramic [THT]"]

nets:
  N1: Part1.A0, P2.cathode
  N2: Part1.A3, P1.cathode
  N3: Part1.IOREF, P1.anode, P2.anode
